# Fritzing sketch fp_Permaboard (saved by Fritzing 0.9.3b)

parts:
  JACK1 = 2.1mm Barrel Jack with Terminal Block
  proto1 = Adafruit_PermaProto_1_4_Board
  T3 = Basic FET N-Channel [part_number=IRLB8721 package="TO220 [THT]"]  # not connected
  T2 = Basic FET N-Channel [part_number=IRLB8721 package="TO220 [THT]"]  # not connected
  T1 = Basic FET N-Channel [part_number=IRLB8721 package="TO220 [THT]"]  # not connected
  R1 = Resistor [tolerance=±5% resistance=1k package="2010 [SMD]"]  # not connected
  D1 = Diode [package=diode-1n4001]
  M3 = DC Motor
  M2 = DC Motor  # not connected
  M1 = DC Motor  # not connected
  R2 = Resistor [tolerance=±5% resistance=1k package="2010 [SMD]"]  # not connected
  R3 = Resistor [tolerance=±5% resistance=1k package="2010 [SMD]"]  # not connected
  D2 = Diode [package=diode-1n4001]
  D3 = Diode [package=diode-1n4001]

nets:
  N1: JACK1.POS, proto1.connectorW1
  N2: JACK1.NEG, proto1.connectorX1
  N3: proto1.connectorA3, proto1.connectorX3
  N4: proto1.connectorA10, proto1.connectorX10
  N5: proto1.connectorA14, M3.pin_2
  N6: proto1.connectorA15, proto1.connectorX14
  N7: proto1.connectorC6, D3.C
  N8: proto1.connectorD5, D2.C
  N9: proto1.connectorD11, D1.C
  N10: proto1.connectorX15, proto1.connectorZ15

notes:
  Motor voltage rated to 7.2V
